# Fritzing sketch Lichtsensor (saved by Fritzing 0.7.12b)
breadboards: 1

parts:
  Arduino1 = Arduino
  LED1 = LED - 5mm [color="Red (633nm)" package="5 mm [THT]"]
  100 = Resistor [tolerance=±5% resistance=100 package=THT]
  R1 = Photocell (LDR) [package=THT]
  R2 = Resistor [tolerance=±5% resistance=10k package=THT]

nets (from the breadboard view):
  N1: Arduino1.GND, LED1.cathode, R2.Pin_1
  N2: Arduino1.D10, 100.Pin_0
  N3: Arduino1.+5V, R1.pin_0
  N4: Arduino1.A3, R1.pin_1, R2.Pin_0
  N5: LED1.anode, 100.Pin_1
