# Fritzing sketch Vibrationssensor (saved by Fritzing 0.7.12b)
breadboards: 1

parts:
  Arduino1 = Arduino
  LED1 = LED - 5mm [color="Red (633nm)" package="5 mm [THT]"]
  100 = Resistor [tolerance=±5% resistance=100 package=THT]
  MIC1 = Microphone

nets:
  N1: Arduino1.GND, LED1.cathode
  N2: Arduino1.+5V, MIC1.pin2
  N3: Arduino1.A0, MIC1.pin1
  N4: LED1.anode, 100.Pin_1
